// Logisim project Lab02_Mux21.circ as structural Verilog: 3 circuits, main circuit lab02
module lab02 (
  input  A1,
  input  B1,
  input  C1,
  input  A2,
  input  B2,
  input  C2,
  input  D2,
  output True1,
  output True2
);

  EQ1 eq1_1 (.In1A(A1), .In1B(B1), .In1C(C1), .Out1(True1));
  Equation_2 equation_2_1 (.in_1(A2), .in_2(B2), .in_3(C2), .in_4(D2), .out_5(True2));
endmodule

module Equation_2 (
  input  in_1,
  input  in_2,
  input  in_3,
  input  in_4,
  output out_5
);

  wire and_1_out, and_2_out, and_3_out, and_4_out;

  and and_1 (and_1_out, ~in_1, ~in_2, in_3, ~in_4);  // AND_Gate
  and and_2 (and_2_out, ~in_1, in_2, in_3, in_4);  // AND_Gate
  and and_3 (and_3_out, in_1, ~in_2, in_3, ~in_4);  // AND_Gate
  and and_4 (and_4_out, in_1, in_2, in_3, ~in_4);  // AND_Gate
  or or_1 (out_5, and_1_out, and_2_out, and_3_out, and_4_out);

  // Notes on the sheet:
  //   A'B'CD'+A'BCD+AB'CD'+ABCD'
endmodule

module EQ1 (
  input  In1A,
  input  In1B,
  input  In1C,
  output Out1
);

  wire and_1_out, and_2_out, and_3_out;

  and and_1 (and_1_out, ~In1A, In1B, ~In1C);  // AND_Gate
  and and_2 (and_2_out, In1A, ~In1B, ~In1C);  // AND_Gate
  and and_3 (and_3_out, In1A, In1B, In1C);
  or or_1 (Out1, and_1_out, and_2_out, and_3_out);

  // Notes on the sheet:
  //   A'BC'+AB'C'+ABC
endmodule
