// Logisim project Lab05_chronogram_timer.circ as structural Verilog: 7 circuits, main circuit main
module main (
  input  Reset
);

  wire clk_out;
  wire [3:0] up_1_up;

  Clock #(.highDuration(4), .lowDuration(4)) clk (.out(clk_out));
  Clock sysclk ();  // open: out
  // Probe on up_1_up
  Hex_Digit_Display hex_digit_display_1 (.value(up_1_up));  // open: dp
  Up up_1 (.clk(clk_out), .rst(Reset), .Up(up_1_up));

  // Notes on the sheet:
  //   Name
  //   Lab 06: Counters
  //   Date
endmodule

module Up (
  input  clk,
  input  rst,
  output [3:0] Up
);

  wire d_ff_1_qn, d_ff_2_qn, d_ff_3_qn, d_ff_4_qn;

  D_Flip_Flop d_ff_1 (.D(d_ff_1_qn), .clk(clk), .Q(Up[0]), .Qn(d_ff_1_qn), .reset(rst));  // open: preset
  D_Flip_Flop d_ff_2 (.D(d_ff_2_qn), .clk(d_ff_1_qn), .Q(Up[1]), .Qn(d_ff_2_qn), .reset(rst));  // open: preset
  D_Flip_Flop d_ff_3 (.D(d_ff_3_qn), .clk(d_ff_2_qn), .Q(Up[2]), .Qn(d_ff_3_qn), .reset(rst));  // open: preset
  D_Flip_Flop d_ff_4 (.D(d_ff_4_qn), .clk(d_ff_3_qn), .Q(Up[3]), .Qn(d_ff_4_qn), .reset(rst));  // open: preset

  // Notes on the sheet:
  //   Asynchronous Four-Bit Up Counter
endmodule

module Down (
  input  clk,
  input  Reset,
  output [3:0] Down
);

  wire d_ff_1_qn, d_ff_2_qn, d_ff_3_qn, d_ff_4_qn;

  D_Flip_Flop d_ff_1 (.D(d_ff_1_qn), .clk(clk), .Q(Down[0]), .Qn(d_ff_1_qn), .preset(Reset));  // open: reset
  D_Flip_Flop d_ff_2 (.D(d_ff_2_qn), .clk(Down[0]), .Q(Down[1]), .Qn(d_ff_2_qn), .preset(Reset));  // open: reset
  D_Flip_Flop d_ff_3 (.D(d_ff_3_qn), .clk(Down[1]), .Q(Down[2]), .Qn(d_ff_3_qn), .preset(Reset));  // open: reset
  D_Flip_Flop d_ff_4 (.D(d_ff_4_qn), .clk(Down[2]), .Q(Down[3]), .Qn(d_ff_4_qn), .preset(Reset));  // open: reset

  // Notes on the sheet:
  //   Asynchronous Four-Bit Down Counter
endmodule

module Decade (
  input  clk,
  input  Reset,
  output [3:0] Decade
);

  wire and_1_out, d_ff_1_qn, d_ff_2_qn, d_ff_3_qn, d_ff_4_qn, or_1_out;

  D_Flip_Flop d_ff_1 (.D(d_ff_1_qn), .clk(clk), .Q(Decade[0]), .Qn(d_ff_1_qn), .reset(or_1_out));  // open: preset
  or or_1 (or_1_out, Reset, and_1_out);
  D_Flip_Flop d_ff_2 (.D(d_ff_2_qn), .clk(d_ff_1_qn), .Q(Decade[1]), .Qn(d_ff_2_qn), .reset(or_1_out));  // open: preset
  D_Flip_Flop d_ff_3 (.D(d_ff_3_qn), .clk(d_ff_2_qn), .Q(Decade[2]), .Qn(d_ff_3_qn), .reset(or_1_out));  // open: preset
  D_Flip_Flop d_ff_4 (.D(d_ff_4_qn), .clk(d_ff_3_qn), .Q(Decade[3]), .Qn(d_ff_4_qn), .reset(or_1_out));  // open: preset
  and and_1 (and_1_out, Decade[3], Decade[1]);

  // Notes on the sheet:
  //   Asynchronous Decade Counter
endmodule

module Ring (
  input  clk,
  input  Reset,
  output [3:0] Ring
);

  D_Flip_Flop d_ff_1 (.D(Ring[3]), .clk(clk), .Q(Ring[0]), .preset(Reset));  // open: Qn, reset
  D_Flip_Flop d_ff_2 (.D(Ring[0]), .clk(clk), .Q(Ring[1]), .reset(Reset));  // open: Qn, preset
  D_Flip_Flop d_ff_3 (.D(Ring[1]), .clk(clk), .Q(Ring[2]), .reset(Reset));  // open: Qn, preset
  D_Flip_Flop d_ff_4 (.D(Ring[2]), .clk(clk), .Q(Ring[3]), .reset(Reset));  // open: Qn, preset

  // Notes on the sheet:
  //   Synchronous Ring Counter
endmodule

module Johnson (
  input  clk,
  input  Reset,
  output [3:0] Johnson
);

  wire d_ff_4_qn;

  D_Flip_Flop d_ff_1 (.D(d_ff_4_qn), .clk(clk), .Q(Johnson[0]), .preset(Reset));  // open: Qn, reset
  D_Flip_Flop d_ff_2 (.D(Johnson[0]), .clk(clk), .Q(Johnson[1]), .reset(Reset));  // open: Qn, preset
  D_Flip_Flop d_ff_3 (.D(Johnson[1]), .clk(clk), .Q(Johnson[2]), .reset(Reset));  // open: Qn, preset
  D_Flip_Flop d_ff_4 (.D(Johnson[2]), .clk(clk), .Q(Johnson[3]), .Qn(d_ff_4_qn), .reset(Reset));  // open: preset

  // Notes on the sheet:
  //   Synchronous Johnson Counter
endmodule

module Universal (
  input  rst,
  input  in_2,
  input  [1:0] in_3,
  output [3:0] out_4
);

  wire clk_out;
  wire [3:0] decade_1_decade, down_1_down, johnson_1_johnson, multiplexer_1_out, ring_1_ring, up_1_up;

  Clock #(.highDuration(4), .lowDuration(4)) clk (.out(clk_out));
  Clock sysclk ();  // open: out
  Up up_1 (.clk(clk_out), .rst(rst), .Up(up_1_up));
  Down down_1 (.clk(clk_out), .Reset(rst), .Down(down_1_down));
  Decade decade_1 (.clk(clk_out), .Reset(rst), .Decade(decade_1_decade));
  Ring ring_1 (.clk(clk_out), .Reset(rst), .Ring(ring_1_ring));
  Johnson johnson_1 (.clk(clk_out), .Reset(rst), .Johnson(johnson_1_johnson));
  Multiplexer #(.select(2), .width(4)) multiplexer_1 (
    .in0(down_1_down), .in1(decade_1_decade), .in2(ring_1_ring), .in3(johnson_1_johnson),
    .out(multiplexer_1_out), .sel(in_3));
  Multiplexer #(.width(4)) multiplexer_2 (.in0(up_1_up), .in1(multiplexer_1_out), .out(out_4), .sel(in_2));
endmodule
